# Fritzing sketch schematique (saved by Fritzing 0.9.6b)
circuit board: 7cm x 5cm
breadboards: 2

parts:
  U1 = ESP32-38PinWide [part_number=ESP32-38PinWide]
  LCD1 = 2.8" SPI TFT Module [part_number=MSP2807]
  Composant1 = GY-BMEP280 Barometric Pressure Sensor - Breakout
  ZS-042_RTC1 = ZS-042 RTC Module
  DHT1 = DHT22 Humidity and Temperature Sensor
  R1 = Resistor [tolerance=±5% resistance=220 package=THT]

nets:
  VCC: U1.3.3, LCD1.pin1, LCD1.pin8, Composant1.VCC, ZS-042_RTC1.VCC, DHT1.VDD, R1.Pin_0
  N1: U1.GPIO26, LCD1.pin4
  N2: U1.GPIO27, LCD1.pin3
  GND: U1.GND, LCD1.pin2, Composant1.GND, ZS-042_RTC1.GND, DHT1.GND
  N3: U1.GPIO16, LCD1.pin5
  N4: U1.GPIO17, DHT1.DATA, R1.Pin_1
  N5: U1.GPIO18, LCD1.pin7
  N6: U1.GPIO19, LCD1.pin9
  N7: U1.GPIO21, Composant1.SDA, ZS-042_RTC1.SDA
  N8: U1.GPIO22, Composant1.SCL, ZS-042_RTC1.SCL
  N9: U1.GPIO23, LCD1.pin6

custom parts:
  ESP32-38PinWide: Generic 38-Pin ESP32 with wide format (only access to one side of pins on a breadboard) based on Stephen Lilley's HiLetgo ESP-WROOM-32 ESP32 ESP-32S Development Board.
  2.8" SPI TFT Module: A generic 2.8 inch LCD TFT 320x240 display with touchscreen and SD card slot. Uses the ILI9341 controller, like the Adafruit displays of this size uses.
  GY-BMEP280 Barometric Pressure Sensor - Breakout: The BME280 is a chip which was originally designed for the next generation of smartphones. It is made up of a very accurate pressure sensor and an associated temperature sensor which helps calibrate the pressure readings. And just for fun they threw in a pretty solid humidity sensor in there as well! So with an I2C connection you have access to enough weather data to make some pretty good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
