# Fritzing sketch station_meteo (saved by Fritzing 0.9.6b)
circuit board: 6.5cm x 5cm
perfboards: 1

parts:
  U1 = ESP32-38PinWide [part_number=ESP32-38PinWide]
  DHT1 = DHT22 Humidity and Temperature Sensor
  Composant1 = GY-BMEP280 Barometric Pressure Sensor - Breakout
  LCD1 = 2.8" SPI TFT Module [part_number=MSP2807]
  R1 = Resistor [tolerance=±5% resistance=220 package=THT]
  R2 = Resistor [tolerance=±5% resistance=220 package=THT]
  ZS-042_RTC1 = ZS-042 RTC Module
  J2 = female pin header, 4 pins [form="♀ (female)"]
  J1 = female pin header, 3 pins [form="♀ (female)"]
  J3 = female pin header, 4 pins [form="♀ (female)"]
  J4 = female pin header, 9 pins [form="♀ (female)"]
  J5 = female pin header, 1 pin [form="♀ (female)"]

nets:
  VCC: U1.3.3, DHT1.VDD, Composant1.VCC, LCD1.pin1, LCD1.pin8, R1.Pin_0, R2.Pin_0, ZS-042_RTC1.VCC, J2.pin1, J1.pin1, J3.pin1, J4.pin1, J4.pin2
  N1: U1.GPIO32, J5.pin1
  N2: U1.GPIO14, DHT1.DATA, R1.Pin_1, J1.pin2
  GND: U1.GND, DHT1.GND, Composant1.GND, LCD1.pin2, ZS-042_RTC1.GND, J2.pin4, J1.pin3, J3.pin4, J4.pin4
  N3: U1.GPIO15, LCD1.pin3, J4.pin9
  N4: U1.GPIO2, LCD1.pin5, J4.pin8
  N5: U1.GPIO0, R2.Pin_1
  N6: U1.GPIO4, LCD1.pin4, J4.pin7
  N7: U1.GPIO18, LCD1.pin7, J4.pin6
  N8: U1.GPIO19, LCD1.pin9, J4.pin5
  N9: U1.GPIO21, Composant1.SDA, ZS-042_RTC1.SDA, J2.pin2, J3.pin2
  N10: U1.GPIO22, Composant1.SCL, ZS-042_RTC1.SCL, J2.pin3, J3.pin3
  N11: U1.GPIO23, LCD1.pin6, J4.pin3

custom parts:
  ESP32-38PinWide: Generic 38-Pin ESP32 with wide format (only access to one side of pins on a breadboard) based on Stephen Lilley's HiLetgo ESP-WROOM-32 ESP32 ESP-32S Development Board.
  GY-BMEP280 Barometric Pressure Sensor - Breakout: The BME280 is a chip which was originally designed for the next generation of smartphones. It is made up of a very accurate pressure sensor and an associated temperature sensor which helps calibrate the pressure readings. And just for fun they threw in a pretty solid humidity sensor in there as well! So with an I2C connection you have access to enough weather data to make some pretty good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
  2.8" SPI TFT Module: A generic 2.8 inch LCD TFT 320x240 display with touchscreen and SD card slot. Uses the ILI9341 controller, like the Adafruit displays of this size uses.
